# Fritzing sketch micModule (saved by Fritzing 0.9.5d)
breadboards: 1

parts:
  Mod1 = KY-026 Flame Sensor Module [package="Breakout board"]
  Part1 = Arduino Uno (Rev3)

nets:
  N1: Mod1.A0, Part1.A0
  N2: Mod1.G, Part1.GND
  N3: Mod1.+, Part1.5V
  N4: Mod1.D0, Part1.D7

custom parts:
  KY-026 Flame Sensor Module: KY-026 Flame Sensor Module reacts in the presence of fire.
